# Fritzing sketch flash-mode (saved by Fritzing 0.9.10b)
breadboards: 1

parts:
  U1 = ESP8266 ESP-01 Upgraded WiFi Module [part_number=ESP8266]
  USBUART1 = PL2303 USB UART Breakout

nets:
  GND: U1.RXD, U1.GPIO_0, U1.GND, USBUART1.GND, USBUART1.RXD
  N1: U1.VCC, U1.RST/GPIO_16, USBUART1.VCCIO
  N2: U1.TXD, USBUART1.TXD

custom parts:
  ESP8266 ESP-01 Upgraded WiFi Module: Upgraded Version ESP-01,all Flash are upgraded to 1M byte.Also support Cloud service remote transmission.
  PL2303 USB UART Breakout: PL2302 Usb Uart Breakout Board with Battery
