# Fritzing sketch work-mode (saved by Fritzing 0.9.10b)
breadboards: 1

parts:
  U1 = ESP8266 ESP-01 Upgraded WiFi Module [part_number=ESP8266]
  DHT11_1 = DHT11 module
  USBUART1 = PL2303 USB UART Breakout

nets:
  VCC: U1.VCC, DHT11_1.VCC, USBUART1.VCCIO
  N1: U1.RST/GPIO_16, DHT11_1.DATA
  GND: U1.GND, DHT11_1.GND, USBUART1.GND

custom parts:
  ESP8266 ESP-01 Upgraded WiFi Module: Upgraded Version ESP-01,all Flash are upgraded to 1M byte.Also support Cloud service remote transmission.
  DHT11 module: DHT11 black pcb module
  PL2303 USB UART Breakout: PL2302 Usb Uart Breakout Board with Battery
